# Fritzing sketch maxclock (saved by Fritzing 1.0.4)
circuit board: 8.46667cm x 5.64444cm
breadboards: 1

parts:
  M1 = DOIT Esp32 DevKit v1 (30 pins long, 11 pins width) [part_number=ESP32S-PIN30]
  J1 = female pin header, 5 pins [form="♀ (female)"]
  R1 = Photocell (LDR) [power=0.25W dark_resistance_@0.01lx=300kΩ light_resistance_@100lx=400Ω luminance=10lx package=THT]
  R2 = Resistor [tolerance=±5% power=0.25W resistance=10k package=THT]
  J2 = Power Jack [package=power_jack_slot]  # not connected

nets:
  N1: M1.3V3, J1.pin1, R1.pin_1
  N2: M1.GND, J1.pin2, R2.Pin_0
  N3: M1.D15, J1.pin4
  N4: M1.VP, R1.pin_0, R2.Pin_1
  N5: M1.D14, J1.pin5
  N6: M1.D13, J1.pin3

notes:
  5v buck
  USB charger

custom parts:
  DOIT Esp32 DevKit v1 (30 pins long, 11 pins width): The DOIT Esp32 DevKit v1 is one of the development board created by DOIT to evaluate the ESP-WROOM-32 module. It is based on the ESP32 microcontroller that boasts Wifi, Bluetooth, Ethernet and Low Power support all in a single chip. (vanepp) made breadboard work, adjusted pin numbering and labels and reduced size of schematic and cleaned up pcb. This chip is 30pins long (2 x15) and 11 pins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
